// Logisim project main.circ as structural Verilog: 8 circuits, main circuit main
module ALU (
  input  [15:0] ALU_in_1,
  input  [15:0] ALU_in_2,
  input  [3:0] Op,
  output [15:0] ALU_out
);

  wire [15:0] adder_1_out, and_1_out, divider_1_out, divider_1_rem, multiplier_1_cout, multiplier_1_out,
       not_1_out, or_1_out, shifter_1_out, shifter_2_out, shifter_3_out, subtractor_1_out, xor_1_out;
  wire [15:10] adder_1_cout;

  Comparator #(.width(16)) comparator_1 (
    .a(ALU_in_1), .b(ALU_in_2), .gt(adder_1_cout[15]), .eq(adder_1_cout[13]), .lt(adder_1_cout[12]));
  Adder #(.width(16)) adder_1 (.a(ALU_in_1), .b(ALU_in_2), .out(adder_1_out), .cout(adder_1_cout[10]));  // open: cin
  Subtractor #(.width(16)) subtractor_1 (.a(ALU_in_1), .b(ALU_in_2), .out(subtractor_1_out));  // open: bin, bout
  Multiplier #(.mode("twosComplement"), .width(16)) multiplier_1 (
    .a(ALU_in_1), .b(ALU_in_2), .out(multiplier_1_out), .cout(multiplier_1_cout));  // open: cin
  Divider #(.mode("twosComplement"), .width(16)) divider_1 (
    .a(ALU_in_1), .b(ALU_in_2), .out(divider_1_out), .rem(divider_1_rem));  // open: upper
  assign and_1_out = ALU_in_1 & ALU_in_2;  // AND_Gate and_1, 16 bits wide
  assign or_1_out = ALU_in_1 | ALU_in_2;  // OR_Gate or_1, 16 bits wide
  assign not_1_out = ~ALU_in_1;  // NOT_Gate not_1, 16 bits wide
  assign xor_1_out = ALU_in_1 ^ ALU_in_2;  // XOR_Gate xor_1, 16 bits wide
  Shifter #(.width(16)) shifter_1 (.in(ALU_in_1), .\dist (ALU_in_2[3:0]), .out(shifter_1_out));
  Shifter #(.shift("lr"), .width(16)) shifter_2 (.in(ALU_in_1), .\dist (ALU_in_2[3:0]), .out(shifter_2_out));
  Shifter #(.shift("ar"), .width(16)) shifter_3 (.in(ALU_in_1), .\dist (ALU_in_2[3:0]), .out(shifter_3_out));
  or or_2 (adder_1_cout[14], adder_1_cout[15], adder_1_cout[13]);
  or or_3 (adder_1_cout[11], adder_1_cout[13], adder_1_cout[12]);
  Multiplexer #(.select(4), .width(16)) multiplexer_1 (
    .in0({adder_1_cout, {10{1'b1}}}), .in1(adder_1_out), .in2(subtractor_1_out), .in3(multiplier_1_out),
    .in4(multiplier_1_cout), .in5(divider_1_out), .in6(divider_1_rem), .in7(and_1_out), .in8(or_1_out),
    .in9(not_1_out), .in10(xor_1_out), .in11(shifter_1_out), .in12(shifter_2_out), .in13(shifter_3_out),
    .out(ALU_out), .sel(Op));  // open: in14, in15

  // Notes on the sheet:
  //   >, >=, =, <, <=, +ov, 1's
endmodule

module Memory (
  input  [15:0] Address,
  input  [15:0] Data,
  input  Clock,
  input  Write,
  output [15:0] Data_out
);

  wire not_1_out;

  RAM #(.addrWidth(16), .dataWidth(16)) ram_1 (
    .addr(Address), .we(Write), .oe(not_1_out), .clk(Clock), .din(Data), .dout(Data_out));
  not not_1 (not_1_out, Write);
endmodule

module PC (
  input  [15:0] PC_in,
  input  Write,
  input  Reset,
  input  Clock,
  output [15:0] Address
);

  Counter #(.max('hffff), .width(16)) counter_1 (
    .clr(Reset), .load(Write), .up(1'b1), .count(1'b1), .clk(Clock), .D(PC_in), .Q(Address));  // open: carry
endmodule

module Instruction_decoder (
  input  [23:0] Instruction,
  input  [6:0] Flags_in,
  output Halt,
  output Write_pc,
  output [7:0] Register_write,
  output Memory_write,
  output [15:0] Operand_2,
  output [2:0] Operand_2_2,
  output [2:0] Operand_2_1,
  output [3:0] ALU_op,
  output [3:0] dbus_mux_select,
  output write_flags
);

  wire and_2_out, and_4_out, and_5_out, nor_3_out, or_2_out;
  wire [6:0] and_6_out, decoder_2_out6;
  wire [7:0] decoder_3_out0, decoder_4_out0;
  wire [10:0] or_3_out;

  nor nor_1 (or_3_out[9], ~Instruction[19], ~Instruction[20], Instruction[21], Instruction[22], Instruction[23]);  // NOR_Gate
  nor nor_2 (or_3_out[10], or_3_out[8], or_3_out[9], or_3_out[7], or_3_out[6], or_3_out[5], or_3_out[4], or_3_out[3], or_3_out[2], or_3_out[1], or_3_out[0]);
  and and_1 (Halt, ~Instruction[23], ~Instruction[22], Instruction[21]);  // AND_Gate
  nor nor_3 (nor_3_out, Instruction[23], Instruction[22], Instruction[21], ~Instruction[20], ~Instruction[19]);  // NOR_Gate
  and and_2 (and_2_out, ~Instruction[23], ~Instruction[20], Instruction[19]);  // AND_Gate
  and and_3 (Memory_write, ~Instruction[23], ~Instruction[21], Instruction[20]);  // AND_Gate
  and and_4 (and_4_out, Instruction[23], Instruction[22], Instruction[21], Instruction[20], Instruction[19]);
  nor nor_4 (write_flags, ~Instruction[23], Instruction[22], Instruction[21], Instruction[20], Instruction[19]);  // NOR_Gate
  and and_5 (and_5_out, Instruction[23], Instruction[22], Instruction[21], Instruction[20], ~Instruction[19]);  // AND_Gate
  or or_1 (or_3_out[8], and_5_out, Write_pc);
  Priority_Encoder #(.select(4)) priority_encoder_1 (
    .in0(or_3_out[0]), .in1(or_3_out[1]), .in2(or_3_out[2]), .in3(or_3_out[3]), .in4(or_3_out[4]),
    .in5(or_3_out[5]), .in6(or_3_out[6]), .in7(or_3_out[7]), .in8(or_3_out[8]), .in9(or_3_out[9]),
    .in10(or_3_out[10]), .out(dbus_mux_select));  // open: in11, in12, in13, in14, in15, gs, en_out, en_in
  or or_2 (or_2_out, Instruction[23], nor_3_out);
  assign or_3_out[7:0] = decoder_3_out0 | decoder_4_out0;  // OR_Gate or_3, 8 bits wide
  Decoder #(.select(3)) decoder_1 (
    .out0(Register_write[0]), .out1(Register_write[1]), .out2(Register_write[2]), .out3(Register_write[3]),
    .out4(Register_write[4]), .out5(Register_write[5]), .out6(Register_write[6]), .out7(Register_write[7]),
    .sel(Instruction[18:16]), .en(or_2_out));
  Decoder #(.select(3)) decoder_2 (
    .out0(decoder_2_out6[6]), .out1(decoder_2_out6[5]), .out2(decoder_2_out6[4]), .out3(decoder_2_out6[3]),
    .out4(decoder_2_out6[2]), .out5(decoder_2_out6[1]), .out6(decoder_2_out6[0]), .sel(Instruction[18:16]),
    .en(and_2_out));  // open: out7
  Decoder #(.select(3)) decoder_3 (
    .out0(decoder_3_out0[0]), .out1(decoder_3_out0[1]), .out2(decoder_3_out0[2]), .out3(decoder_3_out0[3]),
    .out4(decoder_3_out0[4]), .out5(decoder_3_out0[5]), .out6(decoder_3_out0[6]), .out7(decoder_3_out0[7]),
    .sel(Instruction[18:16]), .en(Memory_write));
  Decoder #(.select(3)) decoder_4 (
    .out0(decoder_4_out0[0]), .out1(decoder_4_out0[1]), .out2(decoder_4_out0[2]), .out3(decoder_4_out0[3]),
    .out4(decoder_4_out0[4]), .out5(decoder_4_out0[5]), .out6(decoder_4_out0[6]), .out7(decoder_4_out0[7]),
    .sel(Instruction[15:13]), .en(and_4_out));
  assign and_6_out = Flags_in & decoder_2_out6;  // AND_Gate and_6, 7 bits wide
  ExactlyOne xor_1 (
    .out(Write_pc), .in0(and_6_out[6]), .in1(and_6_out[5]), .in2(and_6_out[4]), .in3(and_6_out[3]),
    .in4(and_6_out[2]), .in5(and_6_out[1]), .in6(and_6_out[0]));

  assign ALU_op = Instruction[22:19];
  assign Operand_2 = Instruction[15:0];
  assign Operand_2_1 = Instruction[15:13];
  assign Operand_2_2 = Instruction[12:10];

  // Notes on the sheet:
  //   1000: cu
  //   1001: memory
  //   1010: ALU
  //   1xxxx: register codes
  //   Rn
  //   Ra
endmodule

module register_array (
  input  [15:0] Data_in,
  input  Clock,
  input  [7:0] Write_signals,
  output [15:0] R0_out,
  output [15:0] R1_out,
  output [15:0] R2_out,
  output [15:0] R3_out,
  output [15:0] R4_out,
  output [15:0] R5_out,
  output [15:0] R6_out,
  output [15:0] R7_out
);

  Register #(.width(16)) R0 (.D(Data_in), .en(Write_signals[0]), .clk(Clock), .Q(R0_out));  // open: clr
  Register #(.width(16)) R1 (.D(Data_in), .en(Write_signals[1]), .clk(Clock), .Q(R1_out));  // open: clr
  Register #(.width(16)) R2 (.D(Data_in), .en(Write_signals[2]), .clk(Clock), .Q(R2_out));  // open: clr
  Register #(.width(16)) R3 (.D(Data_in), .en(Write_signals[3]), .clk(Clock), .Q(R3_out));  // open: clr
  Register #(.width(16)) R4 (.D(Data_in), .en(Write_signals[4]), .clk(Clock), .Q(R4_out));  // open: clr
  Register #(.width(16)) R5 (.D(Data_in), .en(Write_signals[5]), .clk(Clock), .Q(R5_out));  // open: clr
  Register #(.width(16)) R6 (.D(Data_in), .en(Write_signals[6]), .clk(Clock), .Q(R6_out));  // open: clr
  Register #(.width(16)) R7 (.D(Data_in), .en(Write_signals[7]), .clk(Clock), .Q(R7_out));  // open: clr
endmodule

module Flags (
  input  Clk,
  input  [15:0] D,
  input  W,
  output [6:0] Q
);

  wire [8:0] register_1_q;

  Register #(.width(16)) register_1 (.D(D), .en(W), .clk(Clk), .Q({Q, register_1_q}));  // open: clr
endmodule

module main (
);

  wire and_1_out, clock_1_out, d_ff_1_q, instruction_decoder_1_halt, instruction_decoder_1_memory_write,
       instruction_decoder_1_write_flags, instruction_decoder_1_write_pc, not_1_out, Power_out, Restart_out;
  wire [2:0] instruction_decoder_1_operand_2_1, instruction_decoder_1_operand_2_2;
  wire [3:0] instruction_decoder_1_alu_op, instruction_decoder_1_dbus_mux_select;
  wire [6:0] flags_1_q;
  wire [7:0] instruction_decoder_1_register_write;
  wire [15:0] alu_1_alu_out, instruction_decoder_1_operand_2, memory_1_data_out, multiplexer_1_out,
       multiplexer_2_out, multiplexer_3_out, pc_1_address, register_array_1_r0_out, register_array_1_r1_out,
       register_array_1_r2_out, register_array_1_r3_out, register_array_1_r4_out, register_array_1_r5_out,
       register_array_1_r6_out, register_array_1_r7_out;
  wire [23:0] instruction_loader_1_instruction;

  D_Flip_Flop d_ff_1 (.D(not_1_out), .clk(Power_out), .Q(d_ff_1_q));  // open: Qn, preset, reset
  Button Power (.out(Power_out));
  Button Restart (.out(Restart_out));
  Clock clock_1 (.out(clock_1_out));
  not not_1 (not_1_out, d_ff_1_q);
  PC pc_1 (
    .PC_in(instruction_decoder_1_operand_2), .Write(instruction_decoder_1_write_pc), .Reset(Restart_out),
    .Clock(and_1_out), .Address(pc_1_address));
  instruction_loader instruction_loader_1 (
    .Address(pc_1_address), .Clk(and_1_out), .Instruction(instruction_loader_1_instruction));
  Flags flags_1 (.Clk(and_1_out), .D(alu_1_alu_out), .W(instruction_decoder_1_write_flags), .Q(flags_1_q));
  and and_1 (and_1_out, clock_1_out, d_ff_1_q, ~instruction_decoder_1_halt);  // AND_Gate
  register_array register_array_1 (
    .Data_in(multiplexer_3_out), .Clock(and_1_out), .Write_signals(instruction_decoder_1_register_write),
    .R0_out(register_array_1_r0_out), .R1_out(register_array_1_r1_out), .R2_out(register_array_1_r2_out),
    .R3_out(register_array_1_r3_out), .R4_out(register_array_1_r4_out), .R5_out(register_array_1_r5_out),
    .R6_out(register_array_1_r6_out), .R7_out(register_array_1_r7_out));
  Memory memory_1 (
    .Address(instruction_decoder_1_operand_2), .Data(multiplexer_3_out), .Clock(and_1_out),
    .Write(instruction_decoder_1_memory_write), .Data_out(memory_1_data_out));
  Instruction_decoder instruction_decoder_1 (
    .Instruction(instruction_loader_1_instruction), .Flags_in(flags_1_q), .Halt(instruction_decoder_1_halt),
    .Write_pc(instruction_decoder_1_write_pc), .Register_write(instruction_decoder_1_register_write),
    .Memory_write(instruction_decoder_1_memory_write), .Operand_2(instruction_decoder_1_operand_2),
    .Operand_2_2(instruction_decoder_1_operand_2_2), .Operand_2_1(instruction_decoder_1_operand_2_1),
    .ALU_op(instruction_decoder_1_alu_op), .dbus_mux_select(instruction_decoder_1_dbus_mux_select),
    .write_flags(instruction_decoder_1_write_flags));
  Multiplexer #(.select(3), .width(16)) multiplexer_1 (
    .in0(register_array_1_r0_out), .in1(register_array_1_r1_out), .in2(register_array_1_r2_out),
    .in3(register_array_1_r3_out), .in4(register_array_1_r4_out), .in5(register_array_1_r5_out),
    .in6(register_array_1_r6_out), .in7(register_array_1_r7_out), .out(multiplexer_1_out),
    .sel(instruction_decoder_1_operand_2_2));
  Multiplexer #(.select(3), .width(16)) multiplexer_2 (
    .in0(register_array_1_r0_out), .in1(register_array_1_r1_out), .in2(register_array_1_r2_out),
    .in3(register_array_1_r3_out), .in4(register_array_1_r4_out), .in5(register_array_1_r5_out),
    .in6(register_array_1_r6_out), .in7(register_array_1_r7_out), .out(multiplexer_2_out),
    .sel(instruction_decoder_1_operand_2_1));
  ALU alu_1 (
    .ALU_in_1(multiplexer_2_out), .ALU_in_2(multiplexer_1_out), .Op(instruction_decoder_1_alu_op),
    .ALU_out(alu_1_alu_out));
  Multiplexer #(.select(4), .width(16)) multiplexer_3 (
    .in0(register_array_1_r0_out), .in1(register_array_1_r1_out), .in2(register_array_1_r2_out),
    .in3(register_array_1_r3_out), .in4(register_array_1_r4_out), .in5(register_array_1_r5_out),
    .in6(register_array_1_r6_out), .in7(register_array_1_r7_out), .in8(instruction_decoder_1_operand_2),
    .in9(memory_1_data_out), .in10(alu_1_alu_out), .out(multiplexer_3_out),
    .sel(instruction_decoder_1_dbus_mux_select));  // open: in11, in12, in13, in14, in15
endmodule

module instruction_loader (
  input  [15:0] Address,
  input  Clk,
  output [23:0] Instruction
);

  wire not_1_out;
  wire [23:0] rom_1_data;

  ROM #(.addrWidth(16), .dataWidth(24)) rom_1 (.addr(Address), .data(rom_1_data));
  Register #(.width(24)) register_1 (.D(rom_1_data), .en(1'b1), .clk(not_1_out), .Q(Instruction));  // open: clr
  not not_1 (not_1_out, Clk);

  // Notes on the sheet:
  //   contents of rom_1 (hex, n*v repeats v):
  //   800000 f00001 f10001 880401 e0003
endmodule
